// Logisim project ALU_Logisim.circ as structural Verilog: 8 circuits, main circuit main
module main (
  input  [8:0] in_1,
  input  [8:0] in_2,
  input  [2:0] in_3,
  output Carry_flag,
  output [8:0] Result,
  output Zero_flag
);

  ALU_Top alu_top_1 (.A(in_1), .B(in_2), .Alu_Control(in_3), .out_4(Carry_flag), .result(Result), .out_6(Zero_flag));
endmodule

module FullAdder (
  input  [8:0] A,
  input  [8:0] B,
  input  [8:0] Cin,
  output [8:0] Cout,
  output [8:0] sum
);

  wire [8:0] and_1_out, and_2_out, xor_1_out;

  assign xor_1_out = A ^ B;  // XOR_Gate xor_1, 9 bits wide
  assign and_1_out = A & B;  // AND_Gate and_1, 9 bits wide
  assign and_2_out = Cin & xor_1_out;  // AND_Gate and_2, 9 bits wide
  assign Cout = and_1_out | and_2_out;  // OR_Gate or_1, 9 bits wide
  assign sum = xor_1_out ^ Cin;  // XOR_Gate xor_2, 9 bits wide

  // Notes on the sheet:
  //   A
  //   B
  //   Cin
  //   Cout
  //   Sum
endmodule

module ALU_Add (
  input  [8:0] A,
  input  [8:0] B,
  output [8:0] sum_out
);

  wire [8:0] fulladder_1_cout, fulladder_2_cout, fulladder_3_cout, fulladder_4_cout, fulladder_5_cout,
       fulladder_6_cout, fulladder_7_cout, fulladder_8_cout;

  FullAdder fulladder_1 (.A(A), .B(B), .Cin({9{1'b0}}), .Cout(fulladder_1_cout), .sum(sum_out));
  FullAdder fulladder_2 (.A(A), .B(B), .Cin(fulladder_1_cout), .Cout(fulladder_2_cout), .sum(sum_out));
  FullAdder fulladder_3 (.A(A), .B(B), .Cin(fulladder_2_cout), .Cout(fulladder_3_cout), .sum(sum_out));
  FullAdder fulladder_4 (.A(A), .B(B), .Cin(fulladder_3_cout), .Cout(fulladder_4_cout), .sum(sum_out));
  FullAdder fulladder_5 (.A(A), .B(B), .Cin(fulladder_4_cout), .Cout(fulladder_5_cout), .sum(sum_out));
  FullAdder fulladder_6 (.A(A), .B(B), .Cin(fulladder_5_cout), .Cout(fulladder_6_cout), .sum(sum_out));
  FullAdder fulladder_7 (.A(A), .B(B), .Cin(fulladder_6_cout), .Cout(fulladder_7_cout), .sum(sum_out));
  FullAdder fulladder_8 (.A(A), .B(B), .Cin(fulladder_7_cout), .Cout(fulladder_8_cout), .sum(sum_out));
  FullAdder fulladder_9 (.A(A), .B(B), .Cin(fulladder_8_cout), .sum(sum_out));  // open: Cout
endmodule

module ALU_Sub (
  input  [8:0] A,
  input  [8:0] B,
  output [8:0] sub_out
);

  wire [8:0] fulladder_1_cout, fulladder_2_cout, fulladder_3_cout, fulladder_4_cout, fulladder_5_cout,
       fulladder_6_cout, fulladder_7_cout, fulladder_8_cout, not_1_out;

  assign not_1_out = ~B;  // NOT_Gate not_1, 9 bits wide
  FullAdder fulladder_1 (.A(A), .B(not_1_out), .Cin({9{1'b0}}), .Cout(fulladder_1_cout), .sum(sub_out));
  FullAdder fulladder_2 (.A(A), .B(not_1_out), .Cin(fulladder_1_cout), .Cout(fulladder_2_cout), .sum(sub_out));
  FullAdder fulladder_3 (.A(A), .B(not_1_out), .Cin(fulladder_2_cout), .Cout(fulladder_3_cout), .sum(sub_out));
  FullAdder fulladder_4 (.A(A), .B(not_1_out), .Cin(fulladder_3_cout), .Cout(fulladder_4_cout), .sum(sub_out));
  FullAdder fulladder_5 (.A(A), .B(not_1_out), .Cin(fulladder_4_cout), .Cout(fulladder_5_cout), .sum(sub_out));
  FullAdder fulladder_6 (.A(A), .B(not_1_out), .Cin(fulladder_5_cout), .Cout(fulladder_6_cout), .sum(sub_out));
  FullAdder fulladder_7 (.A(A), .B(not_1_out), .Cin(fulladder_6_cout), .Cout(fulladder_7_cout), .sum(sub_out));
  FullAdder fulladder_8 (.A(A), .B(not_1_out), .Cin(fulladder_7_cout), .Cout(fulladder_8_cout), .sum(sub_out));
  FullAdder fulladder_9 (.A(A), .B(not_1_out), .Cin(fulladder_8_cout), .sum(sub_out));  // open: Cout
endmodule

module ALU_Logic (
  input  [8:0] A,
  input  [8:0] B,
  output [8:0] And_out,
  output [8:0] Or_out
);

  assign And_out = A & B;  // AND_Gate and_1, 9 bits wide
  assign Or_out = A | B;  // OR_Gate or_1, 9 bits wide
endmodule

module ALU_ShiftL (
  input  [8:0] A,
  output [8:0] sll_out
);


  assign sll_out = {A[7:0], 1'b0};
endmodule

module ALU_ShiftR (
  input  [8:0] A,
  output [8:0] slr_out
);


  assign slr_out = {A[7:0], 1'b0};
endmodule

module ALU_Top (
  input  [8:0] A,
  input  [8:0] B,
  input  [2:0] Alu_Control,
  output out_4,
  output [8:0] result,
  output out_6
);

  wire [8:0] alu_add_1_sum_out, alu_logic_1_and_out, alu_logic_1_or_out, alu_shiftl_1_sll_out,
       alu_shiftr_1_slr_out, alu_sub_1_sub_out;

  ALU_Add alu_add_1 (.A(A), .B(B), .sum_out(alu_add_1_sum_out));
  ALU_Logic alu_logic_1 (.A(A), .B(B), .And_out(alu_logic_1_and_out), .Or_out(alu_logic_1_or_out));
  ALU_Sub alu_sub_1 (.A(A), .B(B), .sub_out(alu_sub_1_sub_out));
  ALU_ShiftL alu_shiftl_1 (.A(A), .sll_out(alu_shiftl_1_sll_out));
  ALU_ShiftR alu_shiftr_1 (.A(A), .slr_out(alu_shiftr_1_slr_out));
  Multiplexer #(.select(3), .width(9)) multiplexer_1 (
    .in0(alu_logic_1_and_out), .in1(alu_logic_1_or_out), .in2(alu_add_1_sum_out), .in3(alu_sub_1_sub_out),
    .in4(alu_shiftl_1_sll_out), .in5(alu_shiftr_1_slr_out), .in6({9{1'b0}}), .out(result), .sel(Alu_Control));  // open: in7
  Comparator #(.width(9)) comparator_1 (.a(result), .b({9{1'b0}}), .eq(out_6));  // open: gt, lt

  assign out_4 = 1'b0;
endmodule
