// Logisim project CLa2.circ as structural Verilog
module CLA (
  input  A,
  input  B,
  input  Cin,
  output S,
  output Cout
);

  wire and_2_out, and_3_out, not_1_out, not_2_out;

  not not_1 (not_1_out, B);
  not not_2 (not_2_out, Cin);
  and and_1 (S, A, not_1_out, not_2_out);
  and and_2 (and_2_out, A, B);
  and and_3 (and_3_out, A, not_1_out, Cin);
  or or_1 (Cout, and_2_out, and_3_out);
endmodule

module RippleCarry (
  input  [3:0] A,
  input  [3:0] B,
  output [3:0] Sum
);

  wire cla_1_cout, cla_2_cout, cla_3_cout;

  CLA cla_1 (.A(A[0]), .B(B[0]), .Cin(1'b0), .S(Sum[0]), .Cout(cla_1_cout));
  CLA cla_2 (.A(A[1]), .B(B[1]), .Cin(cla_1_cout), .S(Sum[1]), .Cout(cla_2_cout));
  CLA cla_3 (.A(A[2]), .B(B[2]), .Cin(cla_2_cout), .S(Sum[2]), .Cout(cla_3_cout));
  CLA cla_4 (.A(A[3]), .B(B[3]), .Cin(cla_3_cout), .S(Sum[3]));  // open: Cout
endmodule
